# Fritzing sketch circuit-schematic (saved by Fritzing 0.9.3b)

parts:
  Part1 = Arduino Mega 2560 (Rev3)
  S1 = H-Bridge with L298N
  M1 = Stepper Motor - Bipolar
  Raspberry_Pi_1 = Raspberry Pi 3 [part_number=RPI-3-V1.2]  # not connected
  VCC1 = Battery block 9V

nets:
  N1: Part1.D11_PWM, S1.IN4
  N2: Part1.D10_PWM, S1.IN3
  N3: Part1.D9_PWM, S1.IN2
  N4: Part1.D8_PWM, S1.IN1
  5V: Part1.5V, S1.5V
  N5: Part1.D2_PWM, S1.ENA
  N6: Part1.D3_PWM, S1.ENB
  N7: S1.12V, VCC1.+
  N8: S1.GND, VCC1.-
  N9: S1.M1-01, M1.A
  N10: S1.M1-02, M1.C
  N11: S1.M2-01, M1.D
  N12: S1.M2-02, M1.B

notes:
  First two wires, green & black for one winding
  Seond pair of wiring for second winding
  OUT1 and OUT2
  OUT3 & OUT4
  PIN 8-11
  PINS TO IN1,IN2,IN3,IN4

custom parts:
  H-Bridge with L298N: h-bridge
